// Logisim project 24_HOURS_DIGITAL CLOCK.circ as structural Verilog: 6 circuits, main circuit mod-10-counter
module mod_10_counter (
  input  clk,
  input  p,
  input  T,
  output Q4,
  output Q3,
  output Q2,
  output Q1
);

  wire and_1_out, and_2_out, and_3_out, and_4_out, or_1_out, or_2_out, or_3_out, or_4_out;

  and and_1 (and_1_out, clk, p);
  or or_1 (or_1_out, and_4_out, T);
  J_K_Flip_Flop j_k_ff_1 (.J(1'b1), .clk(and_1_out), .K(1'b1), .Q(Q4), .reset(or_1_out));  // open: Qn, preset, en
  or or_2 (or_2_out, T, and_4_out);
  and and_2 (and_2_out, Q4, Q3);
  J_K_Flip_Flop j_k_ff_2 (.J(Q4), .clk(and_1_out), .K(Q4), .Q(Q3), .reset(or_2_out));  // open: Qn, preset, en
  J_K_Flip_Flop j_k_ff_3 (
    .J(and_2_out), .clk(and_1_out), .K(and_2_out), .Q(Q2), .reset(or_3_out));  // open: Qn, preset, en
  or or_3 (or_3_out, T, and_4_out);
  and and_3 (and_3_out, and_2_out, Q2);
  J_K_Flip_Flop j_k_ff_4 (
    .J(and_3_out), .clk(and_1_out), .K(and_3_out), .Q(Q1), .reset(or_4_out));  // open: Qn, preset, en
  or or_4 (or_4_out, and_4_out, T);
  and and_4 (and_4_out, Q1, Q3);
endmodule

module binary_to_7_segment (
  input  q1,
  input  q2,
  input  q3,
  input  q4,
  output a,
  output b,
  output c,
  output d,
  output e,
  output f,
  output g
);

  wire and_1_out, and_2_out, and_3_out, and_4_out, and_5_out, and_6_out, and_7_out, and_8_out, and_9_out,
       and_10_out, and_11_out, and_12_out, and_13_out, and_14_out, and_15_out, and_16_out, not_1_out,
       not_2_out, not_3_out, not_4_out, not_5_out, not_6_out, not_7_out, not_8_out, not_9_out, not_10_out,
       not_11_out, not_12_out, not_13_out, not_14_out, not_15_out, not_16_out, not_17_out, not_18_out,
       not_19_out, not_20_out, not_21_out;

  not not_1 (not_1_out, q2);
  and and_1 (and_1_out, not_1_out, not_2_out);
  not not_2 (not_2_out, q4);
  and and_2 (and_2_out, q2, q4);
  not not_3 (not_3_out, q2);
  not not_4 (not_4_out, q3);
  and and_3 (and_3_out, not_4_out, not_5_out);
  not not_5 (not_5_out, q4);
  and and_4 (and_4_out, q3, q4);
  not not_6 (not_6_out, q3);
  or or_1 (c, not_6_out, q4, q2);
  not not_7 (not_7_out, q2);
  and and_5 (and_5_out, not_7_out, not_8_out);
  not not_8 (not_8_out, q4);
  not not_9 (not_9_out, q2);
  and and_6 (and_6_out, not_9_out, q3);
  and and_7 (and_7_out, q3, not_10_out);
  not not_10 (not_10_out, q4);
  not not_11 (not_11_out, q3);
  and and_8 (and_8_out, q2, not_11_out, q4);
  not not_12 (not_12_out, q2);
  and and_9 (and_9_out, not_12_out, not_13_out);
  not not_13 (not_13_out, q4);
  and and_10 (and_10_out, q3, not_14_out);
  not not_14 (not_14_out, q4);
  not not_15 (not_15_out, q3);
  and and_11 (and_11_out, not_15_out, not_16_out);
  not not_16 (not_16_out, q4);
  and and_12 (and_12_out, q2, not_17_out);
  not not_17 (not_17_out, q3);
  and and_13 (and_13_out, q2, not_18_out);
  not not_18 (not_18_out, q4);
  not not_19 (not_19_out, q2);
  and and_14 (and_14_out, not_19_out, q3);
  and and_15 (and_15_out, q2, not_20_out);
  not not_20 (not_20_out, q3);
  and and_16 (and_16_out, q2, not_21_out);
  not not_21 (not_21_out, q4);
  or or_2 (a, and_1_out, q3, and_2_out, q1);
  or or_3 (b, not_3_out, and_3_out, and_4_out);
  or or_4 (d, and_5_out, and_6_out, and_7_out, and_8_out, q1);
  or or_5 (e, and_9_out, and_10_out);
  or or_6 (f, and_11_out, and_12_out, and_13_out, q1);
  or or_7 (g, and_14_out, and_15_out, and_16_out, q1);
endmodule

module mod_6_counter (
  input  clk,
  input  p,
  input  T,
  output Q4,
  output Q3,
  output Q2,
  output Q1
);

  wire and_1_out, and_2_out, and_3_out, and_4_out, or_1_out;

  and and_1 (and_1_out, clk, p);
  J_K_Flip_Flop j_k_ff_1 (.J(1'b1), .clk(and_1_out), .K(1'b1), .Q(Q4), .reset(or_1_out));  // open: Qn, preset, en
  and and_2 (and_2_out, Q4, Q3);
  J_K_Flip_Flop j_k_ff_2 (.J(Q4), .clk(and_1_out), .K(Q4), .Q(Q3), .reset(or_1_out));  // open: Qn, preset, en
  J_K_Flip_Flop j_k_ff_3 (
    .J(and_2_out), .clk(and_1_out), .K(and_2_out), .Q(Q2), .reset(or_1_out));  // open: Qn, preset, en
  or or_1 (or_1_out, and_4_out, T);
  and and_3 (and_3_out, and_2_out, Q2);
  J_K_Flip_Flop j_k_ff_4 (
    .J(and_3_out), .clk(and_1_out), .K(and_3_out), .Q(Q1), .reset(or_1_out));  // open: Qn, preset, en
  and and_4 (and_4_out, Q2, Q3);
endmodule

module main (
);

  wire and_1_out, and_2_out, and_3_out, and_4_out, and_5_out, and_6_out, binary_to_7_segment_1_a,
       binary_to_7_segment_1_b, binary_to_7_segment_1_c, binary_to_7_segment_1_d, binary_to_7_segment_1_e,
       binary_to_7_segment_1_f, binary_to_7_segment_1_g, binary_to_7_segment_2_a, binary_to_7_segment_2_b,
       binary_to_7_segment_2_c, binary_to_7_segment_2_d, binary_to_7_segment_2_e, binary_to_7_segment_2_f,
       binary_to_7_segment_2_g, binary_to_7_segment_3_a, binary_to_7_segment_3_b, binary_to_7_segment_3_c,
       binary_to_7_segment_3_d, binary_to_7_segment_3_e, binary_to_7_segment_3_f, binary_to_7_segment_3_g,
       binary_to_7_segment_4_a, binary_to_7_segment_4_b, binary_to_7_segment_4_c, binary_to_7_segment_4_d,
       binary_to_7_segment_4_e, binary_to_7_segment_4_f, binary_to_7_segment_4_g, binary_to_7_segment_5_a,
       binary_to_7_segment_5_b, binary_to_7_segment_5_c, binary_to_7_segment_5_d, binary_to_7_segment_5_e,
       binary_to_7_segment_5_f, binary_to_7_segment_5_g, binary_to_7_segment_6_a, binary_to_7_segment_6_b,
       binary_to_7_segment_6_c, binary_to_7_segment_6_d, binary_to_7_segment_6_e, binary_to_7_segment_6_f,
       binary_to_7_segment_6_g, clock_out, M_2_out, M_3_out, M_4_out, M_out, mod_2_counter_1_q1,
       mod_2_counter_1_q2, mod_6_counter_1_q1, mod_6_counter_1_q2, mod_6_counter_1_q3, mod_6_counter_1_q4,
       mod_6_counter_2_q1, mod_6_counter_2_q2, mod_6_counter_2_q3, mod_6_counter_2_q4, mod_10_counter_1_q1,
       mod_10_counter_1_q2, mod_10_counter_1_q3, mod_10_counter_1_q4, mod_10_counter_2_q1,
       mod_10_counter_2_q2, mod_10_counter_2_q3, mod_10_counter_2_q4, or_1_out, or_2_out, or_3_out, or_4_out,
       or_5_out, resetting_hours_1_q1, resetting_hours_1_q2, resetting_hours_1_q3, resetting_hours_1_q4;

  binary_to_7_segment binary_to_7_segment_1 (
    .q1(1'b0), .q2(1'b0), .q3(mod_2_counter_1_q1), .q4(mod_2_counter_1_q2), .a(binary_to_7_segment_1_a),
    .b(binary_to_7_segment_1_b), .c(binary_to_7_segment_1_c), .d(binary_to_7_segment_1_d),
    .e(binary_to_7_segment_1_e), .f(binary_to_7_segment_1_f), .g(binary_to_7_segment_1_g));
  or or_1 (or_1_out, and_2_out, and_1_out);
  _7_Segment_Display u_7_segment_display_1 (
    .g(binary_to_7_segment_1_g), .f(binary_to_7_segment_1_f), .a(binary_to_7_segment_1_a),
    .b(binary_to_7_segment_1_b), .e(binary_to_7_segment_1_e), .d(binary_to_7_segment_1_d),
    .c(binary_to_7_segment_1_c));  // open: dp
  mod_2_counter mod_2_counter_1 (
    .Clk(or_5_out), .P(or_1_out), .T(M_3_out), .Q2(mod_2_counter_1_q2), .Q1(mod_2_counter_1_q1));
  _7_Segment_Display u_7_segment_display_2 (
    .g(binary_to_7_segment_2_g), .f(binary_to_7_segment_2_f), .a(binary_to_7_segment_2_a),
    .b(binary_to_7_segment_2_b), .e(binary_to_7_segment_2_e), .d(binary_to_7_segment_2_d),
    .c(binary_to_7_segment_2_c));  // open: dp
  and and_1 (and_1_out, resetting_hours_1_q1, resetting_hours_1_q3);
  or or_2 (or_2_out, and_2_out, M_3_out);
  binary_to_7_segment binary_to_7_segment_2 (
    .q1(resetting_hours_1_q1), .q2(resetting_hours_1_q2), .q3(resetting_hours_1_q3),
    .q4(resetting_hours_1_q4), .a(binary_to_7_segment_2_a), .b(binary_to_7_segment_2_b),
    .c(binary_to_7_segment_2_c), .d(binary_to_7_segment_2_d), .e(binary_to_7_segment_2_e),
    .f(binary_to_7_segment_2_f), .g(binary_to_7_segment_2_g));
  or or_3 (or_3_out, and_3_out, M_out);
  LED led_1 (.in(1'b1));
  LED led_2 (.in(1'b1));
  resetting_hours resetting_hours_1 (
    .clk(or_5_out), .p(or_3_out), .Q4(resetting_hours_1_q4), .Q3(resetting_hours_1_q3),
    .Q2(resetting_hours_1_q2), .Q1(resetting_hours_1_q1), .reset_hour(or_2_out));
  and and_2 (and_2_out, mod_2_counter_1_q1, resetting_hours_1_q2);
  and and_3 (and_3_out, mod_6_counter_1_q2, mod_6_counter_1_q3);
  Button M (.out(M_out));
  _7_Segment_Display u_7_segment_display_3 (
    .g(binary_to_7_segment_3_g), .f(binary_to_7_segment_3_f), .a(binary_to_7_segment_3_a),
    .b(binary_to_7_segment_3_b), .e(binary_to_7_segment_3_e), .d(binary_to_7_segment_3_d),
    .c(binary_to_7_segment_3_c));  // open: dp
  binary_to_7_segment binary_to_7_segment_3 (
    .q1(mod_6_counter_1_q1), .q2(mod_6_counter_1_q2), .q3(mod_6_counter_1_q3), .q4(mod_6_counter_1_q4),
    .a(binary_to_7_segment_3_a), .b(binary_to_7_segment_3_b), .c(binary_to_7_segment_3_c),
    .d(binary_to_7_segment_3_d), .e(binary_to_7_segment_3_e), .f(binary_to_7_segment_3_f),
    .g(binary_to_7_segment_3_g));
  _7_Segment_Display u_7_segment_display_4 (
    .g(binary_to_7_segment_4_g), .f(binary_to_7_segment_4_f), .a(binary_to_7_segment_4_a),
    .b(binary_to_7_segment_4_b), .e(binary_to_7_segment_4_e), .d(binary_to_7_segment_4_d),
    .c(binary_to_7_segment_4_c));  // open: dp
  and and_4 (and_4_out, mod_10_counter_1_q1, mod_10_counter_1_q3);
  mod_6_counter mod_6_counter_1 (
    .clk(or_5_out), .p(and_4_out), .T(M_3_out), .Q4(mod_6_counter_1_q4), .Q3(mod_6_counter_1_q3),
    .Q2(mod_6_counter_1_q2), .Q1(mod_6_counter_1_q1));
  binary_to_7_segment binary_to_7_segment_4 (
    .q1(mod_10_counter_1_q1), .q2(mod_10_counter_1_q2), .q3(mod_10_counter_1_q3), .q4(mod_10_counter_1_q4),
    .a(binary_to_7_segment_4_a), .b(binary_to_7_segment_4_b), .c(binary_to_7_segment_4_c),
    .d(binary_to_7_segment_4_d), .e(binary_to_7_segment_4_e), .f(binary_to_7_segment_4_f),
    .g(binary_to_7_segment_4_g));
  Button M_2 (.out(M_2_out));
  or or_4 (or_4_out, M_2_out, and_5_out);
  and and_5 (and_5_out, mod_6_counter_2_q2, mod_6_counter_2_q3);
  mod_10_counter mod_10_counter_1 (
    .clk(or_5_out), .p(or_4_out), .T(M_3_out), .Q4(mod_10_counter_1_q4), .Q3(mod_10_counter_1_q3),
    .Q2(mod_10_counter_1_q2), .Q1(mod_10_counter_1_q1));
  LED led_3 (.in(1'b1));
  LED led_4 (.in(1'b1));
  _7_Segment_Display u_7_segment_display_5 (
    .g(binary_to_7_segment_5_g), .f(binary_to_7_segment_5_f), .a(binary_to_7_segment_5_a),
    .b(binary_to_7_segment_5_b), .e(binary_to_7_segment_5_e), .d(binary_to_7_segment_5_d),
    .c(binary_to_7_segment_5_c));  // open: dp
  binary_to_7_segment binary_to_7_segment_5 (
    .q1(mod_6_counter_2_q1), .q2(mod_6_counter_2_q2), .q3(mod_6_counter_2_q3), .q4(mod_6_counter_2_q4),
    .a(binary_to_7_segment_5_a), .b(binary_to_7_segment_5_b), .c(binary_to_7_segment_5_c),
    .d(binary_to_7_segment_5_d), .e(binary_to_7_segment_5_e), .f(binary_to_7_segment_5_f),
    .g(binary_to_7_segment_5_g));
  mod_6_counter mod_6_counter_2 (
    .clk(or_5_out), .p(and_6_out), .T(M_3_out), .Q4(mod_6_counter_2_q4), .Q3(mod_6_counter_2_q3),
    .Q2(mod_6_counter_2_q2), .Q1(mod_6_counter_2_q1));
  _7_Segment_Display u_7_segment_display_6 (
    .g(binary_to_7_segment_6_g), .f(binary_to_7_segment_6_f), .a(binary_to_7_segment_6_a),
    .b(binary_to_7_segment_6_b), .e(binary_to_7_segment_6_e), .d(binary_to_7_segment_6_d),
    .c(binary_to_7_segment_6_c));  // open: dp
  and and_6 (and_6_out, mod_10_counter_2_q3, mod_10_counter_2_q1);
  binary_to_7_segment binary_to_7_segment_6 (
    .q1(mod_10_counter_2_q1), .q2(mod_10_counter_2_q2), .q3(mod_10_counter_2_q3), .q4(mod_10_counter_2_q4),
    .a(binary_to_7_segment_6_a), .b(binary_to_7_segment_6_b), .c(binary_to_7_segment_6_c),
    .d(binary_to_7_segment_6_d), .e(binary_to_7_segment_6_e), .f(binary_to_7_segment_6_f),
    .g(binary_to_7_segment_6_g));
  mod_10_counter mod_10_counter_2 (
    .clk(or_5_out), .p(1'b1), .T(M_3_out), .Q4(mod_10_counter_2_q4), .Q3(mod_10_counter_2_q3),
    .Q2(mod_10_counter_2_q2), .Q1(mod_10_counter_2_q1));
  or or_5 (or_5_out, M_4_out, clock_out);
  Button M_3 (.out(M_3_out));
  _7_Segment_Display u_7_segment_display_7 (.g(1'b1), .f(1'b1), .e(1'b1), .c(1'b1));  // open: a, b, d, dp
  Button M_4 (.out(M_4_out));
  Clock clock (.out(clock_out));
  _7_Segment_Display u_7_segment_display_8 (.g(1'b1), .e(1'b1));  // open: f, a, b, d, c, dp
  _7_Segment_Display u_7_segment_display_9 (.g(1'b1), .f(1'b1), .a(1'b1), .d(1'b1), .c(1'b1));  // open: b, e, dp

  // Notes on the sheet:
  //   A
  //   B
  //   B->MOD 2 COUNTER
  //   C->RESETTING HOURS
  //   D-> MOD 6 COUNTER
  //   A
  //   C
  //   A -> BINARY TO 7-SEGMENT DECODER
  //   SET HOURS
  //   A
  //   D
  //   SET
  //   MINUTES
  //   24 HOUR DIGITAL CLOCK-SYNCHRONOUS APPROACH
  //   A
  //   E
  //   E->MOD 10 COUNTER
  //   A
  //   D
  //   A
  //   E
  //   RESET BUTTON
  //   SET SECONDS
endmodule

module mod_2_counter (
  input  Clk,
  input  P,
  input  T,
  output Q2,
  output Q1
);

  wire and_1_out, and_2_out, or_1_out;

  and and_1 (and_1_out, Clk, P);
  J_K_Flip_Flop j_k_ff_1 (.J(1'b1), .clk(and_1_out), .K(1'b1), .Q(Q2), .reset(or_1_out));  // open: Qn, preset, en
  or or_1 (or_1_out, and_2_out, T);
  J_K_Flip_Flop j_k_ff_2 (.J(Q2), .clk(and_1_out), .K(Q2), .Q(Q1), .reset(or_1_out));  // open: Qn, preset, en
  and and_2 (and_2_out, Q2, Q1);
endmodule

module resetting_hours (
  input  clk,
  input  reset_hour,
  input  p,
  output Q4,
  output Q3,
  output Q2,
  output Q1
);

  wire and_1_out, and_2_out, and_3_out, and_4_out, or_1_out;

  J_K_Flip_Flop j_k_ff_1 (.J(1'b1), .clk(and_1_out), .K(1'b1), .Q(Q4), .reset(or_1_out));  // open: Qn, preset, en
  and and_1 (and_1_out, clk, p);
  J_K_Flip_Flop j_k_ff_2 (.J(Q4), .clk(and_1_out), .K(Q4), .Q(Q3), .reset(or_1_out));  // open: Qn, preset, en
  and and_2 (and_2_out, Q4, Q3);
  and and_3 (and_3_out, and_2_out, Q2);
  J_K_Flip_Flop j_k_ff_3 (
    .J(and_2_out), .clk(and_1_out), .K(and_2_out), .Q(Q2), .reset(or_1_out));  // open: Qn, preset, en
  J_K_Flip_Flop j_k_ff_4 (
    .J(and_3_out), .clk(and_1_out), .K(and_3_out), .Q(Q1), .reset(or_1_out));  // open: Qn, preset, en
  or or_1 (or_1_out, and_4_out, reset_hour);
  and and_4 (and_4_out, Q3, Q1);
endmodule
